# Fritzing sketch mains_power_failure_detection (saved by Fritzing 0.9.10b)
circuit board: 8.46667cm x 5.64444cm

parts:
  Part1 = Adafruit PowerBoost 1000C [part_number="Adafruit #2465"]
  Raspberry_Pi_1 = Raspberry Pi 3 [part_number=RPI-3-V1.2]
  R1 = Resistor [tolerance=±5% power=0.25 resistance=1000 package=THT]
  R2 = Resistor [tolerance=±5% power=0.25 resistance=660 package=THT]
  S3 = Toggle Switch [package=THT]
  Part2 = Lithium Ion Polymer Battery 3.7v 350mAh [part_number=2750]  # not connected

nets:
  GND: Part1.GND, Raspberry_Pi_1.GND, R1.Pin_0, S3.L2
  N1: Part1.VBUS, R2.Pin_1
  N2: Part1.VBAT, S3.L1
  N3: Part1.ENABLE, S3.COM
  N4: Part1.5.0V, Raspberry_Pi_1.5V
  N5: Raspberry_Pi_1.GIPO17, R1.Pin_1, R2.Pin_0

custom parts:
  Adafruit PowerBoost 1000C: PowerBoost 1000C is the perfect power supply for your portable project! With a built-in load-sharing battery charger circuit, you'll be able to keep your power-hungry project running even while recharging the battery! This little DC/DC boost converter module can be powered by any 3.7V LiIon/LiPoly battery, and convert the battery output to 5.2V DC for running your 5V projects.
  Lithium Ion Polymer Battery 3.7v 350mAh: Lithium ion polymer (also known as 'lipo' or 'lipoly') batteries are thin, light and powerful. The output ranges from 4.2V when completely charged to 3.7V. This battery has a capacity of 350mAh for a total of about 1.3 Wh. The batteries come pre-attached with a genuine 2-pin JST-PH connector as shown and include the necessary protection circuitry.
